// Logisim project CPU.circ as structural Verilog: 2 circuits, main circuit ALU
module main (
  input  [7:0] in_1
);

  Register #(.width(4)) register_1 ();  // open: D, en, Q, clk, clr
  Adder adder_1 ();  // open: a, b, out, cin, cout
endmodule

module ALU (
  input  Y,
  input  [3:0] A,
  input  [3:0] B,
  input  [3:0] OP,
  output [3:0] OUT,
  output [3:0] FLAG
);

  wire [3:0] adder_1_out, adder_2_out, and_1_out, buffer_1_out, buffer_2_out, divider_1_out,
       multiplier_1_out, not_1_out, or_1_out, shifter_1_out, shifter_2_out, xor_1_out, xor_5_out, xor_9_out;

  xor xor_1 (xor_1_out[0], Y, B[0]);
  xor xor_2 (xor_1_out[1], Y, B[1]);
  xor xor_3 (xor_1_out[2], Y, B[2]);
  xor xor_4 (xor_1_out[3], Y, B[3]);
  xor xor_5 (xor_5_out[0], Y, 1'b1);
  xor xor_6 (xor_5_out[1], Y, 1'b0);
  xor xor_7 (xor_5_out[2], Y, 1'b0);
  xor xor_8 (xor_5_out[3], Y, 1'b0);
  Adder #(.width(4)) adder_1 (.a(A), .b(xor_1_out), .out(adder_1_out), .cin(Y), .cout(FLAG[1]));
  Adder #(.width(4)) adder_2 (.a(A), .b(xor_5_out), .out(adder_2_out), .cin(Y));  // open: cout
  Multiplier #(.width(4)) multiplier_1 (.a(A), .b(B), .out(multiplier_1_out));  // open: cin, cout
  Divider #(.width(4)) divider_1 (.a(A), .b(B), .out(divider_1_out));  // open: upper, rem
  Shifter #(.width(4)) shifter_1 (.in(A), .\dist (B[1:0]), .out(shifter_1_out));
  Shifter #(.width(4), .shift("lr")) shifter_2 (.in(A), .\dist (B[1:0]), .out(shifter_2_out));
  assign buffer_1_out = A;  // Buffer buffer_1, 4 bits wide
  assign buffer_2_out = B;  // Buffer buffer_2, 4 bits wide
  assign not_1_out = ~A;  // NOT_Gate not_1, 4 bits wide
  assign and_1_out = A & B;  // AND_Gate and_1, 4 bits wide
  assign or_1_out = A | B;  // OR_Gate or_1, 4 bits wide
  assign xor_9_out = A ^ B;  // XOR_Gate xor_9, 4 bits wide
  Comparator #(.width(4), .mode("unsigned")) comparator_1 (.a(A), .b(B), .eq(FLAG[0]));  // open: gt, lt
  Comparator #(.width(4)) comparator_2 (.a(adder_2_out), .b(4'b0000), .eq(FLAG[2]));  // open: gt, lt
  Comparator #(.width(4)) comparator_3 (.a(A), .b(B), .gt(FLAG[3]));  // open: eq, lt
  Multiplexer #(.select(4), .width(4), .enable("false")) multiplexer_1 (
    .in0(buffer_1_out), .in1(adder_1_out), .in2(adder_2_out), .in3(multiplier_1_out), .in4(divider_1_out),
    .in5(shifter_1_out), .in6(shifter_2_out), .in7(not_1_out), .in8(and_1_out), .in10(or_1_out),
    .in12(xor_9_out), .in15(buffer_2_out), .out(OUT), .sel(OP));  // open: in9, in11, in13, in14

  // Notes on the sheet:
  //   ADD/SUB
  //   INC/DEC
  //   DIV
  //   SHIFT LEFT
  //   SHIFT RIGHT
endmodule
